// Logisim project ULA.circ as structural Verilog: 30 circuits, main circuit meiosomador
module meiosomador (
  input  in_1,
  input  in_2,
  output out_3,
  output out_4
);

  xor Soma (out_3, in_1, in_2);
  and Carry_In (out_4, in_1, in_2);
endmodule

module somadorcompleto (
  input  Cin,
  input  A,
  input  B,
  output \Saída_Soma ,
  output Cout
);

  wire A___B_out, A___Cin_out, B__Cin_out, Soma_out;

  xor Soma (Soma_out, A, B);
  and A___B (A___B_out, A, B);
  and A___Cin (A___Cin_out, A, Cin);
  and B__Cin (B__Cin_out, B, Cin);
  xor plus_Cin (\Saída_Soma , Cin, Soma_out);
  or Out (Cout, A___B_out, A___Cin_out, B__Cin_out);
endmodule

module MUX32 (
  input  E0,
  input  E1,
  input  E2,
  input  E3,
  input  E4,
  input  E5,
  input  E6,
  input  E7,
  input  E8,
  input  E9,
  input  E10,
  input  E11,
  input  E12,
  input  E13,
  input  E14,
  input  E15,
  input  E16,
  input  E17,
  input  E18,
  input  E19,
  input  E20,
  input  E21,
  input  E22,
  input  E23,
  input  E24,
  input  E25,
  input  E26,
  input  E27,
  input  E28,
  input  E29,
  input  E30,
  input  E31,
  input  [4:0] in_33,
  output out_34
);

  wire mux16_1_out_21, mux16_2_out_21;

  MUX16 mux16_1 (
    .E0(E0), .E1(E1), .E2(E2), .E3(E3), .in_5(E4), .E5(E5), .E6(E6), .E7(E7), .E8(E8), .E9(E9), .E10(E10),
    .E11(E11), .in_13(E12), .E13(E13), .E14(E14), .E15(E15), .C(in_33[3]), .D(in_33[2]), .A(in_33[1]),
    .B(in_33[0]), .out_21(mux16_1_out_21));
  MUX16 mux16_2 (
    .E0(E16), .E1(E17), .E2(E18), .E3(E19), .in_5(E20), .E5(E21), .E6(E22), .E7(E23), .E8(E24), .E9(E25),
    .E10(E26), .E11(E27), .in_13(E28), .E13(E29), .E14(E30), .E15(E31), .C(in_33[3]), .D(in_33[2]),
    .A(in_33[1]), .B(in_33[0]), .out_21(mux16_2_out_21));
  MUX2 mux2_1 (.E0(mux16_1_out_21), .E1(mux16_2_out_21), .E(in_33[4]), .out_4(out_34));
endmodule

module MUX4 (
  input  in_1,
  input  in_2,
  input  in_3,
  input  in_4,
  input  in_5,
  input  in_6,
  output out_7
);

  wire and_1_out, and_2_out, and_3_out, and_4_out;

  and and_1 (and_1_out, in_1, ~in_5, ~in_6);  // AND_Gate
  and and_2 (and_2_out, in_2, ~in_5, in_6);  // AND_Gate
  and and_3 (and_3_out, in_3, in_5, ~in_6);  // AND_Gate
  and and_4 (and_4_out, in_4, in_5, in_6);
  or or_1 (out_7, and_1_out, and_2_out, and_3_out, and_4_out);
endmodule

module MUX16 (
  input  E0,
  input  E1,
  input  E2,
  input  E3,
  input  in_5,
  input  E5,
  input  E6,
  input  E7,
  input  E8,
  input  E9,
  input  E10,
  input  E11,
  input  in_13,
  input  E13,
  input  E14,
  input  E15,
  input  C,
  input  D,
  input  A,
  input  B,
  output out_21
);

  wire mux8_1_out_12, mux8_2_out_12;

  MUX8 mux8_1 (
    .E0(E0), .E1(E1), .E2(E2), .E3(E3), .E4(in_5), .E5(E5), .E6(E6), .E7(E7), .B(D), .C(A), .A(B),
    .out_12(mux8_1_out_12));
  MUX8 mux8_2 (
    .E0(E8), .E1(E9), .E2(E10), .E3(E11), .E4(in_13), .E5(E13), .E6(E14), .E7(E15), .B(D), .C(A), .A(B),
    .out_12(mux8_2_out_12));
  MUX2 mux2_1 (.E0(mux8_1_out_12), .E1(mux8_2_out_12), .E(C), .out_4(out_21));
endmodule

module MUX2 (
  input  E0,
  input  E1,
  input  E,
  output out_4
);

  wire and_1_out, and_2_out;

  and and_1 (and_1_out, E0, ~E);  // AND_Gate
  and and_2 (and_2_out, E1, E);
  or or_1 (out_4, and_1_out, and_2_out);
endmodule

module \CélulaULA  (
  input  A,
  input  B,
  input  Cin,
  input  [4:0] in_4,
  output Cout,
  output out_6
);

  wire and_1_out, or_1_out, \somadorcompleto_1_saída_soma , xor_1_out;

  and and_1 (and_1_out, A, B);
  or or_1 (or_1_out, A, B);
  xor xor_1 (xor_1_out, A, B);
  somadorcompleto somadorcompleto_1 (
    .Cin(Cin), .A(A), .B(B), .\Saída_Soma (\somadorcompleto_1_saída_soma ), .Cout(Cout));
  MUX32 mux32_1 (
    .E0(and_1_out), .E1(or_1_out), .E2(\somadorcompleto_1_saída_soma ), .E3(xor_1_out), .E4(B), .E5(B),
    .E6(B), .in_33(in_4), .out_34(out_6));  // open: E7, E8, E9, E10, E11, E12, E13, E14, E15, E16, E17, E18, E19, E20, E21, E22, E23, E24, E25, E26, E27, E28, E29, E30, E31
endmodule

module ULA (
  input  [31:0] in_1,
  input  [31:0] in_2,
  input  in_3,
  input  in_4,
  input  in_5
);

  wire slldetect_1_out_2;
  wire [29:0] undriven;
  wire [31:0] shiftleftarit_1_out_3, shiftleftlogico_1_out_3, shiftrightarit_1_out_3,
       shiftrightlogico_1_out_3;

  SLLDetect slldetect_1 (.out_2(slldetect_1_out_2));  // open: in_1
  ShiftRightLogico shiftrightlogico_1 (.in_1(shiftleftlogico_1_out_3), .in_2(in_3), .out_3(shiftrightlogico_1_out_3));
  ShiftLeftLogico shiftleftlogico_1 (.in_1(in_2), .in_2(slldetect_1_out_2), .out_3(shiftleftlogico_1_out_3));
  ShiftLeftArit shiftleftarit_1 (.in_1(shiftrightarit_1_out_3), .in_2(in_5), .out_3(shiftleftarit_1_out_3));
  ShiftRightArit shiftrightarit_1 (.in_1(shiftrightlogico_1_out_3), .Shift(in_4), .out_3(shiftrightarit_1_out_3));
  \CélulaULA  \célulaula_1  (.A(undriven[29]), .B(shiftleftarit_1_out_3[30]));  // open: Cout, in_4, Cin, out_6
  \CélulaULA  \célulaula_2  (.B(shiftleftarit_1_out_3[31]));  // open: Cout, A, in_4, Cin, out_6
  \CélulaULA  \célulaula_3  (.A(undriven[28]), .B(shiftleftarit_1_out_3[29]));  // open: Cout, in_4, Cin, out_6
  \CélulaULA  \célulaula_4  (.A(undriven[27]), .B(shiftleftarit_1_out_3[28]));  // open: Cout, in_4, Cin, out_6
  \CélulaULA  \célulaula_5  (.A(undriven[26]), .B(shiftleftarit_1_out_3[27]));  // open: Cout, in_4, Cin, out_6
  \CélulaULA  \célulaula_6  (.A(undriven[25]), .B(shiftleftarit_1_out_3[26]));  // open: Cout, in_4, Cin, out_6
  \CélulaULA  \célulaula_7  (.A(undriven[24]), .B(shiftleftarit_1_out_3[25]));  // open: Cout, in_4, Cin, out_6
  \CélulaULA  \célulaula_8  (.A(undriven[23]), .B(shiftleftarit_1_out_3[24]));  // open: Cout, in_4, Cin, out_6
  \CélulaULA  \célulaula_9  (.A(undriven[21]), .B(shiftleftarit_1_out_3[22]));  // open: Cout, in_4, Cin, out_6
  \CélulaULA  \célulaula_10  (.A(undriven[22]), .B(shiftleftarit_1_out_3[23]));  // open: Cout, in_4, Cin, out_6
  \CélulaULA  \célulaula_11  (.A(undriven[20]), .B(shiftleftarit_1_out_3[21]));  // open: Cout, in_4, Cin, out_6
  \CélulaULA  \célulaula_12  (.A(undriven[19]), .B(shiftleftarit_1_out_3[20]));  // open: Cout, in_4, Cin, out_6
  \CélulaULA  \célulaula_13  (.B(shiftleftarit_1_out_3[18]));  // open: Cout, A, in_4, Cin, out_6
  \CélulaULA  \célulaula_14  (.A(undriven[18]), .B(shiftleftarit_1_out_3[19]));  // open: Cout, in_4, Cin, out_6
  \CélulaULA  \célulaula_15  (.A(undriven[16]), .B(shiftleftarit_1_out_3[16]));  // open: Cout, in_4, Cin, out_6
  \CélulaULA  \célulaula_16  (.B(shiftleftarit_1_out_3[17]));  // open: Cout, A, in_4, Cin, out_6
  \CélulaULA  \célulaula_17  (.A(undriven[15]), .B(shiftleftarit_1_out_3[15]));  // open: Cout, in_4, Cin, out_6
  \CélulaULA  \célulaula_18  (.A(undriven[14]), .B(shiftleftarit_1_out_3[14]));  // open: Cout, in_4, Cin, out_6
  \CélulaULA  \célulaula_19  (.A(undriven[13]), .B(shiftleftarit_1_out_3[13]));  // open: Cout, in_4, Cin, out_6
  \CélulaULA  \célulaula_20  (.A(undriven[12]), .B(shiftleftarit_1_out_3[12]));  // open: Cout, in_4, Cin, out_6
  \CélulaULA  \célulaula_21  (.A(undriven[10]), .B(shiftleftarit_1_out_3[10]));  // open: Cout, in_4, Cin, out_6
  \CélulaULA  \célulaula_22  (.A(undriven[11]), .B(shiftleftarit_1_out_3[11]));  // open: Cout, in_4, Cin, out_6
  \CélulaULA  \célulaula_23  (.A(undriven[9]), .B(shiftleftarit_1_out_3[9]));  // open: Cout, in_4, Cin, out_6
  \CélulaULA  \célulaula_24  (.A(undriven[8]), .B(shiftleftarit_1_out_3[8]));  // open: Cout, in_4, Cin, out_6
  \CélulaULA  \célulaula_25  (.A(undriven[7]), .B(shiftleftarit_1_out_3[7]));  // open: Cout, in_4, Cin, out_6
  \CélulaULA  \célulaula_26  (.A(undriven[6]), .B(shiftleftarit_1_out_3[6]));  // open: Cout, in_4, Cin, out_6
  \CélulaULA  \célulaula_27  (.A(undriven[5]), .B(shiftleftarit_1_out_3[5]));  // open: Cout, in_4, Cin, out_6
  \CélulaULA  \célulaula_28  (.A(undriven[4]), .B(shiftleftarit_1_out_3[4]));  // open: Cout, in_4, Cin, out_6
  \CélulaULA  \célulaula_29  (.A(undriven[3]), .B(shiftleftarit_1_out_3[3]));  // open: Cout, in_4, Cin, out_6
  \CélulaULA  \célulaula_30  (.A(undriven[2]), .B(shiftleftarit_1_out_3[2]));  // open: Cout, in_4, Cin, out_6
  \CélulaULA  \célulaula_31  (.A(undriven[0]), .B(shiftleftarit_1_out_3[0]));  // open: Cout, in_4, Cin, out_6
  \CélulaULA  \célulaula_32  (.A(undriven[1]), .B(shiftleftarit_1_out_3[1]));  // open: Cout, in_4, Cin, out_6
endmodule

module MUX8 (
  input  E0,
  input  E1,
  input  E2,
  input  E3,
  input  E4,
  input  E5,
  input  E6,
  input  E7,
  input  B,
  input  C,
  input  A,
  output out_12
);

  wire mux4_1_out_7, mux4_2_out_7;

  MUX4 mux4_1 (.in_1(E0), .in_2(E1), .in_3(E2), .in_4(E3), .in_5(C), .in_6(A), .out_7(mux4_1_out_7));
  MUX4 mux4_2 (.in_1(E4), .in_2(E5), .in_3(E6), .in_4(E7), .in_5(C), .in_6(A), .out_7(mux4_2_out_7));
  MUX2 mux2_1 (.E0(mux4_1_out_7), .E1(mux4_2_out_7), .E(B), .out_4(out_12));
endmodule

module ShiftLeftLogico (
  input  [31:0] in_1,
  input  in_2,
  output [31:0] out_3
);

  MUX2maisbits mux2maisbits_1 (.E0(in_1), .E1({in_1[30:0], 1'b0}), .E(in_2), .out_4(out_3));
endmodule

module MUX2maisbits (
  input  [31:0] E0,
  input  [31:0] E1,
  input  E,
  output [31:0] out_4
);

  wire [31:0] and_1_out, and_2_out;

  assign and_1_out = E0 & ~{32{E}};  // AND_Gate and_1, 32 bits wide
  assign and_2_out = E1 & {32{E}};  // AND_Gate and_2, 32 bits wide
  assign out_4 = and_1_out | and_2_out;  // OR_Gate or_1, 32 bits wide
endmodule

module ShiftRightLogico (
  input  [31:0] in_1,
  input  in_2,
  output [31:0] out_3
);

  MUX2maisbits mux2maisbits_1 (.E0(in_1), .E1({1'b0, in_1[31:1]}), .E(in_2), .out_4(out_3));
endmodule

module ShiftRightArit (
  input  [31:0] in_1,
  input  Shift,
  output [31:0] out_3
);

  MUX2maisbits mux2maisbits_1 (.E0(in_1), .E1({{2{in_1[31]}}, in_1[30:1]}), .E(Shift), .out_4(out_3));
endmodule

module ShiftLeftArit (
  input  [31:0] in_1,
  input  in_2,
  output [31:0] out_3
);

  MUX2maisbits mux2maisbits_1 (.E0(in_1), .E1({in_1[30:0], in_1[0]}), .E(in_2), .out_4(out_3));
endmodule

module SLLDetect (
  input  [4:0] in_1,
  output out_2
);

  and and_1 (out_2, ~in_1[0], ~in_1[1], in_1[2], ~in_1[3], ~in_1[4]);  // AND_Gate

  // Notes on the sheet:
  //   00000 = and
  //   00001 = or
  //   00010 = soma
  //   00011 = xor
  //   00100 = sll
  //   00101 = outra op1
  //   00110 = outra op2
endmodule

module ANDDetect (
  input  [4:0] in_1,
  output out_2
);

  and and_1 (out_2, ~in_1[0], ~in_1[1], ~in_1[2], ~in_1[3], ~in_1[4]);  // AND_Gate
endmodule

module ORDetect (
  input  [4:0] in_1,
  output out_2
);

  and and_1 (out_2, in_1[0], ~in_1[1], ~in_1[2], ~in_1[3], ~in_1[4]);  // AND_Gate
endmodule

module SOMADetect (
  input  [4:0] in_1,
  output out_2
);

  and and_1 (out_2, ~in_1[0], in_1[1], ~in_1[2], ~in_1[3], ~in_1[4]);  // AND_Gate
endmodule

module XORDETECT (
  input  [4:0] in_1,
  output out_2
);

  and and_1 (out_2, in_1[0], in_1[1], ~in_1[2], ~in_1[3], ~in_1[4]);  // AND_Gate
endmodule

module extra1Detect (
  input  [4:0] in_1,
  output out_2
);

  and and_1 (out_2, in_1[0], ~in_1[1], in_1[2], ~in_1[3], ~in_1[4]);  // AND_Gate
endmodule

module extra2Detect (
  input  [4:0] in_1,
  output out_2
);

  and and_1 (out_2, ~in_1[0], in_1[1], in_1[2], ~in_1[3], ~in_1[4]);  // AND_Gate
endmodule

module extra3Detect (
  input  [4:0] in_1,
  output out_2
);

  and and_1 (out_2, in_1[0], in_1[1], in_1[2], ~in_1[3], ~in_1[4]);  // AND_Gate
endmodule

module extra4Detect (
  input  [4:0] in_1,
  output out_2
);

  and and_1 (out_2, ~in_1[0], ~in_1[1], ~in_1[2], in_1[3], ~in_1[4]);  // AND_Gate
endmodule

module extra5Detect (
  input  [4:0] in_1,
  output out_2
);

  and and_1 (out_2, in_1[0], ~in_1[1], ~in_1[2], in_1[3], ~in_1[4]);  // AND_Gate
endmodule

module extra6Detect (
  input  [4:0] in_1,
  output out_2
);

  and and_1 (out_2, ~in_1[0], in_1[1], ~in_1[2], in_1[3], ~in_1[4]);  // AND_Gate
endmodule

module extra7Detecy (
  input  [4:0] in_1,
  output out_2
);

  and and_1 (out_2, in_1[0], in_1[1], ~in_1[2], in_1[3], ~in_1[4]);  // AND_Gate
endmodule

module extra8Detect (
  input  [4:0] in_1,
  output out_2
);

  and and_1 (out_2, ~in_1[0], ~in_1[1], in_1[2], in_1[3], ~in_1[4]);  // AND_Gate
endmodule

module extra9Detect (
  input  [4:0] in_1,
  output out_2
);

  and and_1 (out_2, in_1[0], ~in_1[1], in_1[2], in_1[3], ~in_1[4]);  // AND_Gate
endmodule

module extra10Detect (
  input  [4:0] in_1,
  output out_2
);

  and and_1 (out_2, ~in_1[0], in_1[1], in_1[2], in_1[3], ~in_1[4]);  // AND_Gate
endmodule

module extra11Detect (
  input  [4:0] in_1,
  output out_2
);

  and and_1 (out_2, in_1[0], in_1[1], in_1[2], in_1[3], ~in_1[4]);  // AND_Gate
endmodule
